# Fritzing sketch SimonDiceSketch (saved by Fritzing 0.9.2b)
breadboards: 1

parts:
  Part1 = Arduino Mega 2560 (Rev3)
  R1 = Resistor [tolerance=±5% resistance=220 package=THT]
  R2 = Resistor [tolerance=±5% resistance=220 package=THT]
  R3 = Resistor [tolerance=±5% resistance=220 package=THT]
  R4 = Resistor [tolerance=±5% resistance=220 package=THT]
  R5 = Resistor [tolerance=±5% resistance=220 package=THT]
  R6 = Resistor [tolerance=±5% resistance=220 package=THT]
  7_Segment1 = 7 Segment Display
  S1 = Pushbutton [package=THT]
  S2 = Pushbutton [package=THT]
  S3 = Pushbutton [package=THT]
  S4 = Pushbutton [package=THT]
  R7 = Resistor [tolerance=±5% resistance=330 package=THT]
  R8 = Resistor [tolerance=±5% resistance=330 package=THT]
  R9 = Resistor [tolerance=±5% resistance=330 package=THT]
  R10 = Resistor [tolerance=±5% resistance=330 package=THT]
  R11 = Resistor [tolerance=±5% resistance=220 package=THT]
  R12 = Resistor [tolerance=±5% resistance=220 package=THT]
  R13 = Resistor [tolerance=±5% resistance=220 package=THT]
  R14 = Resistor [tolerance=±5% resistance=220 package=THT]
  R15 = Resistor [tolerance=±5% resistance=220 package=THT]
  R16 = Resistor [tolerance=±5% resistance=220 package=THT]
  R17 = Resistor [tolerance=±5% resistance=220 package=THT]
  R18 = Resistor [tolerance=±5% resistance=220 package=THT]
  LED1 = LED - 5mm [color="Red (633nm)" package="5 mm [THT]"]
  LED2 = LED - 5mm [color="Yellow (595nm)" package="5 mm [THT]"]
  LED3 = LED - 5mm [color="Green (555nm)" package="5 mm [THT]"]
  LED4 = LED - 5mm [color="Red (633nm)" package="5 mm [THT]"]
  LED5 = LED - 5mm [color="Yellow (595nm)" package="5 mm [THT]"]
  LED6 = LED - 5mm [color="Green (555nm)" package="5 mm [THT]"]
  R19 = Resistor [tolerance=±5% resistance=220 package=THT]
  R20 = Resistor [tolerance=±5% resistance=220 package=THT]
  LED7 = LED - 5mm [color="Red (633nm)" package="5 mm [THT]"]
  LED8 = LED - 5mm [color="Green (555nm)" package="5 mm [THT]"]
  R21 = Resistor [tolerance=±5% resistance=220 package=THT]
  LED9 = LED - 5mm [color="Yellow (595nm)" package="5 mm [THT]"]

nets:
  N1: Part1.D13_PWM, R1.Pin_0
  N2: Part1.D12_PWM, R2.Pin_0
  N3: Part1.D11_PWM, R3.Pin_0
  N4: Part1.D10_PWM, R4.Pin_0
  N5: Part1.D9_PWM, R5.Pin_0
  N6: Part1.D8_PWM, R6.Pin_0
  N7: Part1.5V, 7_Segment1.common_anode, S1.leg0, S2.leg0, S3.leg0, S4.leg0
  N8: Part1.GND, R7.Pin_1, R8.Pin_1, R9.Pin_1, R10.Pin_1, LED1.cathode, LED2.cathode, LED3.cathode, LED4.cathode, LED5.cathode, LED6.cathode, LED7.anode, LED8.anode, LED9.cathode
  N9: Part1.D4_PWM, S4.leg1, R10.Pin_0
  N10: Part1.D5_PWM, S3.leg1, R9.Pin_0
  N11: Part1.D6_PWM, S2.leg1, R8.Pin_0
  N12: Part1.D7_PWM, S1.leg1, R7.Pin_0
  N13: Part1.D22, R18.Pin_1
  N14: Part1.D24, R17.Pin_1
  N15: Part1.D26, R15.Pin_1
  N16: Part1.D28, R16.Pin_1
  N17: Part1.D31, R19.Pin_0
  N18: Part1.D33, R20.Pin_0
  N19: Part1.D50, R13.Pin_0
  N20: Part1.D51, R12.Pin_0
  N21: Part1.D52, R14.Pin_0
  N22: Part1.D53, R11.Pin_0
  N23: R1.Pin_1, LED1.anode
  N24: R2.Pin_1, LED2.anode
  N25: R3.Pin_1, LED3.anode
  N26: R4.Pin_1, LED4.anode
  N27: R5.Pin_1, LED5.anode
  N28: R6.Pin_1, LED6.anode
  N29: 7_Segment1.Segment_G, R15.Pin_0
  N30: 7_Segment1.Segment_F, R16.Pin_0
  N31: 7_Segment1.Segment_E, R14.Pin_1
  N32: 7_Segment1.Segment_D, R13.Pin_1
  N33: 7_Segment1.Segment_DP, R11.Pin_1
  N34: 7_Segment1.Segment_C, R12.Pin_1
  N35: 7_Segment1.Segment_B, R18.Pin_0
  N36: 7_Segment1.Segment_A, R17.Pin_0
  N37: R19.Pin_1, LED7.cathode
  N38: R20.Pin_1, LED8.cathode
  N39: R21.Pin_1, LED9.anode
